# Fritzing sketch Sublpresse (saved by Fritzing 0.9.2b)

parts:
  Part1 = Arduino Mega 2560 (Rev3)  # not connected
  LCD1 = LCD screen  # not connected
  Part2 = Arduino Prototyping Shield
  U1 = MAX6675 [package=so08]  # not connected
  U2 = MAX6675 [package=so08]  # not connected
  IC2 = L293D [package=THT]

nets:
  N1: Part2.N$16, IC2.Enable_2
  N2: Part2.N$235, IC2.+V
  N3: Part2.N$236, IC2.In_4
  N4: Part2.N$239, IC2.Out_4_(_Controlled_by_Enable_2_)
  N5: Part2.N$259, IC2.Enable_1
  N6: Part2.N$261, IC2.In_1
  N7: Part2.N$262, IC2.Out_1_(_Controlled_by_Enable_1_)
  N8: Part2.N$263, Part2.N$267, Part2.N$268, Part2.N$298, IC2.0V
  N9: Part2.N$269, IC2.Out_3_(_Controlled_by_Enable_2_)
  N10: Part2.N$297, IC2.Out_2_(_Controlled_by_Enable_1_)
  N11: Part2.N$299, IC2.In_2
  N12: Part2.N$305, IC2.In_3
  N13: Part2.N$319, IC2.+Vmotor
