# Fritzing sketch Sublpresse_2 (saved by Fritzing 0.9.2b)
stripboards: 2

parts:
  LCD1 = LCD screen
  Part2 = Arduino Prototyping Shield
  U1 = MAX6675 [package=so08]
  U2 = MAX6675 [package=so08]
  S1 = Pushbutton [package="[SMD]"]
  S2 = Pushbutton [package="[SMD]"]
  S3 = Pushbutton [package="[SMD]"]
  S4 = Pushbutton [package="[SMD]"]
  S5 = Pushbutton [package="[SMD]"]
  S6 = Pushbutton [package="[SMD]"]
  U3 = RELAY-SOLIDSTATE [package=relay-s108t02]
  U4 = RELAY-SOLIDSTATE [package=relay-s108t02]
  L1 = Solenoid
  U5 = Transformer [package=transformer]
  R1 = TRIMPOT [package=3362u-2]
  U6 = TLP621 [package=THT]
  U7 = TLP621 [package=THT]
  U8 = TLP621 [package=THT]
  J1 = Peltier Element
  J2 = Peltier Element
  Part3 = Arduino Uno (Rev3)  # not connected

nets:
  VSS: LCD1.VSS, LCD1.R/W, LCD1.LED-, Part2.GND, Part2.N$117, Part2.N$230, Part2.N$235, Part2.N$238, Part2.N$239, Part2.N$267, Part2.N$312, U1.VSS, U2.VSS, S1.Pin_1, S1.Pin_2, S2.Pin_1, S2.Pin_2, S3.Pin_1, S3.Pin_2, S4.Pin_1, S4.Pin_2, S5.Pin_1, S5.Pin_2, S6.Pin_1, S6.Pin_2, R1.CW, U6.Pin_2, U7.Pin_2, U8.Pin_2
  VDD: LCD1.VDD, LCD1.LED+, Part2.+5V, Part2.N$396, U1.VDD, U2.VDD, R1.CCW
  N1: LCD1.V0, Part2.N$393, R1.WIPER
  N2: LCD1.RS, Part2.D0(RX)
  N3: LCD1.E, Part2.D1(TX)
  N4: LCD1.DB4, Part2.D2
  N5: LCD1.DB5, Part2.D3
  N6: LCD1.DB6, Part2.D4
  N7: LCD1.DB7, Part2.D5
  N8: Part2.A2, S4.Pin_3, S4.Pin_4
  N9: Part2.D8, U1.CS
  N10: Part2.D9, U2.CS
  N11: Part2.D10, Part2.N$269, U8.Pin_1
  N12: Part2.D11, Part2.N$268, U7.Pin_1
  N13: Part2.D12, Part2.N$236, U6.Pin_1
  N14: Part2.D6, U1.SCK, U2.SCK
  N15: Part2.D7, U1.MISO, U2.MISO
  N16: Part2.A0, S5.Pin_3, S5.Pin_4
  N17: Part2.A1, S3.Pin_4
  N18: Part2.A3, S1.Pin_3, S1.Pin_4
  N19: Part2.A4, S2.Pin_3, S2.Pin_4
  N20: Part2.RESET, S6.Pin_3, S6.Pin_4
  N21: Part2.N$69, Part2.N$259, Part2.N$262, Part2.N$274, Part2.N$283, Part2.N$298, U5.4, U6.Pin_3, U7.Pin_3, U8.Pin_3
  N22: Part2.N$261, U4.+, U6.Pin_4
  N23: Part2.N$263, U3.+, U7.Pin_4
  N24: Part2.N$297, L1.pin2, U8.Pin_4
  N25: U1.T-, J1.pin1
  N26: U1.T+, J1.pin2
  N27: U2.T-, J2.pin1
  N28: U2.T+, J2.pin2
  N29: U3.-, U4.-, L1.pin1, U5.1
